# Fritzing sketch MPU6050_diagram_setup (saved by Fritzing 0.9.9b)

parts:
  Part1 = Arduino Leonardo (Rev3b)
  Part2 = InvenSense MPU6050
  VCC1 = Battery block 9V  # not connected

nets:
  N1: Part1.D2/SDA, Part2.INT
  3V3: Part1.3V3, Part2.VCC
  GND: Part1.GND, Part2.GND, Part2.AD0
  N2: Part1.A4, Part2.SDA
  N3: Part1.A5, Part2.SCL
